// Logisim project ex4.circ as structural Verilog: 5 circuits, main circuit RotRight
module RotRight (
  input  [15:0] INPUT0,
  input  [3:0] AMOUNT,
  output [15:0] OUTPUT0
);

  wire [15:0] R1, R2, R3, R4, R5, R6, R7, R8, R9, R10, R11, R12, R13, R14, R15;

  rot1 rot1_1 (.out_2(R1), .in_1(INPUT0));
  rot2 rot2_1 (.out_2(R2), .in_1(INPUT0));
  rot4 rot4_1 (.out_2(R4), .in_1(INPUT0));
  rot8 rot8_1 (.out_2(R8), .in_1(INPUT0));
  rot1 rot1_2 (.out_2(R7), .in_1(R6));
  rot8 rot8_2 (.out_2(R14), .in_1(R6));
  rot1 rot1_3 (.out_2(R11), .in_1(R10));
  rot2 rot2_2 (.out_2(R12), .in_1(R10));
  rot8 rot8_3 (.out_2(R13), .in_1(R5));
  rot4 rot4_2 (.out_2(R5), .in_1(R1));
  rot2 rot2_3 (.out_2(R3), .in_1(R1));
  rot4 rot4_3 (.out_2(R6), .in_1(R2));
  rot1 rot1_4 (.out_2(R9), .in_1(R8));
  rot2 rot2_4 (.out_2(R10), .in_1(R8));
  rot8 rot8_4 (.out_2(R15), .in_1(R7));
  Multiplexer #(.enable("false"), .select(4), .width(16)) multiplexer_1 (
    .in0(INPUT0), .in1(R1), .in2(R2), .in3(R3), .in4(R4), .in5(R5), .in6(R6), .in7(R7), .in8(R8), .in9(R9),
    .in10(R10), .in11(R11), .in12(R12), .in13(R13), .in14(R14), .in15(R15), .out(OUTPUT0), .sel(AMOUNT));
endmodule

module rot1 (
  input  [15:0] in_1,
  output [15:0] out_2
);


  assign out_2 = {in_1[0], in_1[15:1]};
endmodule

module rot2 (
  input  [15:0] in_1,
  output [15:0] out_2
);


  assign out_2 = {in_1[1:0], in_1[15:2]};
endmodule

module rot4 (
  input  [15:0] in_1,
  output [15:0] out_2
);


  assign out_2 = {in_1[3:0], in_1[15:4]};
endmodule

module rot8 (
  input  [15:0] in_1,
  output [15:0] out_2
);


  assign out_2 = {in_1[7:0], in_1[15:8]};
endmodule
