// Logisim project control-logic.circ as structural Verilog: 1 circuit, main circuit control_logic
module control_logic (
  input  [31:0] Instruction,
  input  BrEq,
  input  BrLt,
  output PCSel,
  output RegWEn,
  output [2:0] ImmSel,
  output BrUn,
  output ASel,
  output BSel,
  output [3:0] ALUSel,
  output MemWEn,
  output [1:0] WBSel
);

  wire and_1_out, and_34_out, and_35_out, and_36_out, and_37_out, and_38_out, and_39_out, auipc, B_TYPE,
       func3_0, func3_1, func3_2, func3_3, func3_4, func3_5, func3_6, func3_7, func7_00, func7_01, func7_20,
       I_TYPE, is_add, is_addi, is_and, is_andi, is_beq, is_bge, is_bgeu, is_blt, is_bltu, is_bne, is_lb,
       is_lh, is_lw, is_mul, is_mulh, is_mulhu, is_or, is_ori, is_sb, is_sh, is_sll, is_slli, is_slt,
       is_slti, is_sra, is_srai, is_srl, is_srli, is_sub, is_sw, is_xor, is_xori, Iw_TYPE, jal, jalr, lui,
       multiplexer_3_out, or_1_out, or_2_out, R_TYPE, S_TYPE, UNCONDITION_JUMP;
  wire [1:0] priority_encoder_1_out;
  wire [4:0] priority_encoder_2_out;
  wire [5:0] bit_extender_1_out, multiplexer_1_out, ROM_INPUT, ROM_INPUT2;
  wire [15:14] rom_1_data;

  Multiplexer #(.enable("false"), .width(6)) multiplexer_1 (
    .in0(ROM_INPUT), .in1(ROM_INPUT2), .out(multiplexer_1_out), .sel(and_1_out));
  and and_1 (and_1_out, Instruction[0], Instruction[1], Instruction[2]);
  ROM #(.addrWidth(6), .dataWidth(16)) rom_1 (
    .addr(multiplexer_1_out), .data({rom_1_data, WBSel, MemWEn, ALUSel, BSel, ASel, BrUn, ImmSel, RegWEn}));
  and and_2 (is_sb, S_TYPE, func3_0);
  and and_3 (is_sh, S_TYPE, func3_1);
  and and_4 (is_sw, S_TYPE, func3_2);
  and and_5 (is_lb, Iw_TYPE, func3_0);
  and and_6 (is_lh, Iw_TYPE, func3_1);
  and and_7 (is_lw, Iw_TYPE, func3_2);
  and and_8 (is_add, R_TYPE, func3_0, func7_00);
  and and_9 (is_mul, R_TYPE, func3_0, func7_01);
  and and_10 (is_sub, R_TYPE, func3_0, func7_20);
  and and_11 (is_sll, R_TYPE, func3_1, func7_00);
  and and_12 (is_mulh, R_TYPE, func3_1, func7_01);
  and and_13 (is_mulhu, R_TYPE, func3_3, func7_01);
  and and_14 (is_slt, R_TYPE, func3_2, func7_00);
  and and_15 (is_xor, R_TYPE, func3_4, func7_00);
  and and_16 (is_srl, R_TYPE, func3_5, func7_00);
  and and_17 (is_sra, R_TYPE, func3_5, func7_20);
  and and_18 (is_or, R_TYPE, func3_6, func7_00);
  and and_19 (is_and, R_TYPE, func3_7, func7_00);
  Multiplexer #(.enable("false")) multiplexer_2 (
    .in0(multiplexer_3_out), .in1(or_2_out), .out(PCSel), .sel(UNCONDITION_JUMP));
  Multiplexer #(.enable("false")) multiplexer_3 (.in0(1'b0), .in1(or_1_out), .out(multiplexer_3_out), .sel(B_TYPE));
  or or_1 (or_1_out, and_34_out, and_35_out, and_36_out, and_37_out, and_38_out, and_39_out);
  or or_2 (or_2_out, jal, jalr);
  and and_20 (is_beq, B_TYPE, func3_0);
  and and_21 (is_bne, B_TYPE, func3_1);
  and and_22 (is_blt, B_TYPE, func3_4);
  and and_23 (is_bge, B_TYPE, func3_5);
  and and_24 (is_bltu, B_TYPE, func3_6);
  and and_25 (is_bgeu, B_TYPE, func3_7);
  and and_26 (is_addi, I_TYPE, func3_0);
  and and_27 (is_slli, I_TYPE, func3_1, func7_00);
  and and_28 (is_slti, I_TYPE, func3_2);
  and and_29 (is_xori, I_TYPE, func3_4);
  and and_30 (is_srli, I_TYPE, func3_5, func7_00);
  and and_31 (is_srai, I_TYPE, func3_5, func7_20);
  and and_32 (is_ori, I_TYPE, func3_6);
  and and_33 (is_andi, I_TYPE, func3_7);
  and and_34 (and_34_out, BrEq, is_beq);
  and and_35 (and_35_out, ~BrEq, is_bne);  // AND_Gate
  and and_36 (and_36_out, BrLt, is_blt);
  and and_37 (and_37_out, ~BrLt, is_bge);  // AND_Gate
  and and_38 (and_38_out, BrLt, is_bltu);
  and and_39 (and_39_out, ~BrLt, is_bgeu);  // AND_Gate
  and and_40 (UNCONDITION_JUMP, Instruction[2], Instruction[6]);
  Comparator #(.mode("unsigned"), .width(7)) comparator_1 (
    .a(Instruction[6:0]), .b(7'b1101111), .eq(jal));  // open: gt, lt
  Comparator #(.mode("unsigned"), .width(7)) comparator_2 (
    .a(Instruction[6:0]), .b(7'b0010111), .eq(auipc));  // open: gt, lt
  Comparator #(.mode("unsigned"), .width(7)) comparator_3 (
    .a(Instruction[6:0]), .b(7'b1100011), .eq(B_TYPE));  // open: gt, lt
  Comparator #(.mode("unsigned"), .width(7)) comparator_4 (
    .a(Instruction[6:0]), .b(7'b0100011), .eq(S_TYPE));  // open: gt, lt
  Comparator #(.mode("unsigned"), .width(7)) comparator_5 (
    .a(Instruction[6:0]), .b(7'b0010011), .eq(I_TYPE));  // open: gt, lt
  Comparator #(.mode("unsigned"), .width(7)) comparator_6 (
    .a(Instruction[6:0]), .b(7'b0110011), .eq(R_TYPE));  // open: gt, lt
  Comparator #(.mode("unsigned"), .width(7)) comparator_7 (
    .a(Instruction[6:0]), .b(7'b0000011), .eq(Iw_TYPE));  // open: gt, lt
  Comparator #(.mode("unsigned"), .width(7)) comparator_8 (
    .a(Instruction[6:0]), .b(7'b1100111), .eq(jalr));  // open: gt, lt
  Comparator #(.mode("unsigned"), .width(7)) comparator_9 (
    .a(Instruction[6:0]), .b(7'b0110111), .eq(lui));  // open: gt, lt
  Comparator #(.width(3)) comparator_10 (.a(Instruction[14:12]), .b(3'b000), .eq(func3_0));  // open: gt, lt
  Comparator #(.width(3)) comparator_11 (.a(Instruction[14:12]), .b(3'b001), .eq(func3_1));  // open: gt, lt
  Comparator #(.width(3)) comparator_12 (.a(Instruction[14:12]), .b(3'b010), .eq(func3_2));  // open: gt, lt
  Comparator #(.width(3)) comparator_13 (.a(Instruction[14:12]), .b(3'b011), .eq(func3_3));  // open: gt, lt
  Comparator #(.width(3)) comparator_14 (.a(Instruction[14:12]), .b(3'b100), .eq(func3_4));  // open: gt, lt
  Comparator #(.width(3)) comparator_15 (.a(Instruction[14:12]), .b(3'b101), .eq(func3_5));  // open: gt, lt
  Comparator #(.width(3)) comparator_16 (.a(Instruction[14:12]), .b(3'b110), .eq(func3_6));  // open: gt, lt
  Comparator #(.width(3)) comparator_17 (.a(Instruction[14:12]), .b(3'b111), .eq(func3_7));  // open: gt, lt
  Comparator #(.width(7)) comparator_18 (.a(Instruction[31:25]), .b({7{1'b0}}), .eq(func7_00));  // open: gt, lt
  Comparator #(.width(7)) comparator_19 (.a(Instruction[31:25]), .b(7'b0000001), .eq(func7_01));  // open: gt, lt
  Comparator #(.width(7)) comparator_20 (.a(Instruction[31:25]), .b(7'b0100000), .eq(func7_20));  // open: gt, lt
  assign bit_extender_1_out = {{4{1'b0}}, priority_encoder_1_out};  // Bit_Extender bit_extender_1
  Priority_Encoder #(.select(2)) priority_encoder_1 (
    .in0(auipc), .in1(lui), .in2(jal), .in3(jalr), .out(priority_encoder_1_out));  // open: gs, en_out, en_in
  Adder #(.width(6)) adder_1 (.a(bit_extender_1_out), .b(6'b100000), .out(ROM_INPUT2));  // open: cin, cout
  Priority_Encoder #(.select(5)) priority_encoder_2 (
    .in0(is_add), .in1(is_mul), .in2(is_sub), .in3(is_sll), .in4(is_mulh), .in5(is_mulhu), .in6(is_slt),
    .in7(is_xor), .in8(is_srl), .in9(is_sra), .in10(is_or), .in11(is_and), .in12(is_lb), .in13(is_lh),
    .in14(is_lw), .in15(is_addi), .in16(is_slli), .in17(is_slti), .in18(is_xori), .in19(is_srli),
    .in20(is_srai), .in21(is_ori), .in22(is_andi), .in23(is_sb), .in24(is_sh), .in25(is_sw), .in26(is_beq),
    .in27(is_bne), .in28(is_blt), .in29(is_bge), .in30(is_bltu), .in31(is_bgeu), .out(priority_encoder_2_out));  // open: gs, en_out, en_in
  assign ROM_INPUT = {{1{1'b0}}, priority_encoder_2_out};  // Bit_Extender bit_extender_2

  // Notes on the sheet:
  //   INPUTS to your circuit
  //   Connect ROM Input here ->
  //   contents of rom_1 (hex, n*v repeats v):
  //   1001 1401 1601 1081 1401 1491 1101 1201 1281 1681 1301 1381 43 43 43 1043 10cf 1143 1243 12cf 16cf
  //   1343 13c3 1844 1844 1844 4*1066 1076 1076 1069 17e9 206b 2043 2043 1000 0 1 1 0 1 0 0 1001 0 1 1 4*0
  //   10 0 1 1 4*0 100 0 1
  //   ROM FOR CONTROL LOGIC
  //   DON'T CHANGE THE LOCATIONS OF THE INPUTS AND OUTPUTS!
  //   This is only if you choose to do the ROM option
  //   CONNECT
  //   WIRE
  //   TO
  //   USE
  //   ROM
  //   OUTPUT from your circuit
  //   Reminder: If using ROM, use combinational logic for PCSel
endmodule
