// Logisim project imm-gen.circ as structural Verilog: 1 circuit, main circuit imm_gen
module imm_gen (
  input  [31:0] Instruction,
  input  [2:0] ImmSel,
  output [31:0] Immediate
);

  wire [31:0] bit_extender_1_out, bit_extender_2_out, bit_extender_3_out, bit_extender_4_out,
       bit_extender_5_out, bit_extender_6_out, shifter_1_out;

  assign bit_extender_1_out = {{20{Instruction[31]}}, Instruction[31:20]};  // Bit_Extender bit_extender_1
  assign bit_extender_2_out = {{20{Instruction[31]}}, {Instruction[31:25], Instruction[11:7]}};  // Bit_Extender bit_extender_2
  assign bit_extender_3_out = {{19{Instruction[31]}}, {Instruction[31], Instruction[7], Instruction[30:25], Instruction[11:8], 1'b0}};  // Bit_Extender bit_extender_3
  assign bit_extender_4_out = {{12{Instruction[31]}}, Instruction[31:12]};  // Bit_Extender bit_extender_4
  assign bit_extender_5_out = {{11{Instruction[31]}}, {Instruction[31], Instruction[19:12], Instruction[20], Instruction[30:21], 1'b0}};  // Bit_Extender bit_extender_5
  assign bit_extender_6_out = {{27{1'b0}}, Instruction[24:20]};  // Bit_Extender bit_extender_6
  Shifter #(.width(32)) shifter_1 (.in(bit_extender_4_out), .\dist (5'b01100), .out(shifter_1_out));
  Multiplexer #(.enable("false"), .select(3), .width(32)) multiplexer_1 (
    .in1(bit_extender_1_out), .in2(bit_extender_2_out), .in3(bit_extender_3_out), .in4(shifter_1_out),
    .in5(bit_extender_5_out), .in7(bit_extender_6_out), .out(Immediate), .sel(ImmSel));  // open: in0, in6

  // Notes on the sheet:
  //   INPUTS to your circuit
  //   DON'T CHANGE THE LOCATIONS OF THE INPUTS AND OUTPUTS!
  //   OUTPUT from your circuit
endmodule
