// Logisim project regfile.circ as structural Verilog: 1 circuit, main circuit regfile
module regfile (
  input  [4:0] ReadReg1,
  input  [4:0] ReadReg2,
  input  [4:0] WriteReg,
  input  [31:0] RegWriteData,
  input  RegWEn,
  input  clk,
  output [31:0] ra,
  output [31:0] sp,
  output [31:0] t0,
  output [31:0] t1,
  output [31:0] t2,
  output [31:0] s0,
  output [31:0] s1,
  output [31:0] a0,
  output [31:0] RegReadData1,
  output [31:0] RegReadData2
);

  wire En0, En1, En2, En3, En4, En5, En6, En7, En8, En9, En10, En11, En12, En13, En14, En15, En16, En17,
       En18, En19, En20, En21, En22, En23, En24, En25, En26, En27, En28, En29, En30, En31;
  wire [31:0] rd0, rd3, rd4, rd11, rd12, rd13, rd14, rd15, rd16, rd17, rd18, rd19, rd20, rd21, rd22, rd23,
       rd24, rd25, rd26, rd27, rd28, rd29, rd30, rd31;

  Demultiplexer #(.enable("false"), .select(5)) demultiplexer_1 (
    .out0(En0), .out1(En1), .out2(En2), .out3(En3), .out4(En4), .out5(En5), .out6(En6), .out7(En7),
    .out8(En8), .out9(En9), .out10(En10), .out11(En11), .out12(En12), .out13(En13), .out14(En14),
    .out15(En15), .out16(En16), .out17(En17), .out18(En18), .out19(En19), .out20(En20), .out21(En21),
    .out22(En22), .out23(En23), .out24(En24), .out25(En25), .out26(En26), .out27(En27), .out28(En28),
    .out29(En29), .out30(En30), .out31(En31), .in(RegWEn), .sel(WriteReg));
  Register #(.width(32)) register_1 (.D({32{1'b0}}), .en(En0), .clk(clk), .Q(rd0));  // open: clr
  Register #(.width(32)) register_2 (.D(RegWriteData), .en(En1), .clk(clk), .Q(ra));  // open: clr
  Register #(.width(32)) register_3 (.D(RegWriteData), .en(En2), .clk(clk), .Q(sp));  // open: clr
  Register #(.width(32)) register_4 (.D(RegWriteData), .en(En3), .clk(clk), .Q(rd3));  // open: clr
  Register #(.width(32)) register_5 (.D(RegWriteData), .en(En4), .clk(clk), .Q(rd4));  // open: clr
  Register #(.width(32)) register_6 (.D(RegWriteData), .en(En5), .clk(clk), .Q(t0));  // open: clr
  Register #(.width(32)) register_7 (.D(RegWriteData), .en(En6), .clk(clk), .Q(t1));  // open: clr
  Register #(.width(32)) register_8 (.D(RegWriteData), .en(En7), .clk(clk), .Q(t2));  // open: clr
  Register #(.width(32)) register_9 (.D(RegWriteData), .en(En8), .clk(clk), .Q(s0));  // open: clr
  Register #(.width(32)) register_10 (.D(RegWriteData), .en(En9), .clk(clk), .Q(s1));  // open: clr
  Register #(.width(32)) register_11 (.D(RegWriteData), .en(En10), .clk(clk), .Q(a0));  // open: clr
  Register #(.width(32)) register_12 (.D(RegWriteData), .en(En11), .clk(clk), .Q(rd11));  // open: clr
  Register #(.width(32)) register_13 (.D(RegWriteData), .en(En12), .clk(clk), .Q(rd12));  // open: clr
  Register #(.width(32)) register_14 (.D(RegWriteData), .en(En13), .clk(clk), .Q(rd13));  // open: clr
  Register #(.width(32)) register_15 (.D(RegWriteData), .en(En14), .clk(clk), .Q(rd14));  // open: clr
  Register #(.width(32)) register_16 (.D(RegWriteData), .en(En15), .clk(clk), .Q(rd15));  // open: clr
  Register #(.width(32)) register_17 (.D(RegWriteData), .en(En16), .clk(clk), .Q(rd16));  // open: clr
  Register #(.width(32)) register_18 (.D(RegWriteData), .en(En17), .clk(clk), .Q(rd17));  // open: clr
  Register #(.width(32)) register_19 (.D(RegWriteData), .en(En18), .clk(clk), .Q(rd18));  // open: clr
  Register #(.width(32)) register_20 (.D(RegWriteData), .en(En19), .clk(clk), .Q(rd19));  // open: clr
  Register #(.width(32)) register_21 (.D(RegWriteData), .en(En20), .clk(clk), .Q(rd20));  // open: clr
  Register #(.width(32)) register_22 (.D(RegWriteData), .en(En21), .clk(clk), .Q(rd21));  // open: clr
  Register #(.width(32)) register_23 (.D(RegWriteData), .en(En22), .clk(clk), .Q(rd22));  // open: clr
  Register #(.width(32)) register_24 (.D(RegWriteData), .en(En23), .clk(clk), .Q(rd23));  // open: clr
  Register #(.width(32)) register_25 (.D(RegWriteData), .en(En24), .clk(clk), .Q(rd24));  // open: clr
  Register #(.width(32)) register_26 (.D(RegWriteData), .en(En25), .clk(clk), .Q(rd25));  // open: clr
  Register #(.width(32)) register_27 (.D(RegWriteData), .en(En26), .clk(clk), .Q(rd26));  // open: clr
  Register #(.width(32)) register_28 (.D(RegWriteData), .en(En27), .clk(clk), .Q(rd27));  // open: clr
  Register #(.width(32)) register_29 (.D(RegWriteData), .en(En28), .clk(clk), .Q(rd28));  // open: clr
  Register #(.width(32)) register_30 (.D(RegWriteData), .en(En29), .clk(clk), .Q(rd29));  // open: clr
  Register #(.width(32)) register_31 (.D(RegWriteData), .en(En30), .clk(clk), .Q(rd30));  // open: clr
  Register #(.width(32)) register_32 (.D(RegWriteData), .en(En31), .clk(clk), .Q(rd31));  // open: clr
  Multiplexer #(.enable("false"), .select(5), .width(32)) multiplexer_1 (
    .in0(rd0), .in1(ra), .in2(sp), .in3(rd3), .in4(rd4), .in5(t0), .in6(t1), .in7(t2), .in8(s0), .in9(s1),
    .in10(a0), .in11(rd11), .in12(rd12), .in13(rd13), .in14(rd14), .in15(rd15), .in16(rd16), .in17(rd17),
    .in18(rd18), .in19(rd19), .in20(rd20), .in21(rd21), .in22(rd22), .in23(rd23), .in24(rd24), .in25(rd25),
    .in26(rd26), .in27(rd27), .in28(rd28), .in29(rd29), .in30(rd30), .in31(rd31), .out(RegReadData1),
    .sel(ReadReg1));
  Multiplexer #(.enable("false"), .select(5), .width(32)) multiplexer_2 (
    .in0(rd0), .in1(ra), .in2(sp), .in3(rd3), .in4(rd4), .in5(t0), .in6(t1), .in7(t2), .in8(s0), .in9(s1),
    .in10(a0), .in11(rd11), .in12(rd12), .in13(rd13), .in14(rd14), .in15(rd15), .in16(rd16), .in17(rd17),
    .in18(rd18), .in19(rd19), .in20(rd20), .in21(rd21), .in22(rd22), .in23(rd23), .in24(rd24), .in25(rd25),
    .in26(rd26), .in27(rd27), .in28(rd28), .in29(rd29), .in30(rd30), .in31(rd31), .out(RegReadData2),
    .sel(ReadReg2));

  // Notes on the sheet:
  //   INPUTS to your circuit
  //   DON'T CHANGE THE LOCATIONS OF THE INPUTS AND OUTPUTS!
  //   These are DEBUG/TEST outputs from your circuit.
  //   OUTPUTS from your circuit
endmodule
